# Fritzing sketch ParkDistance (saved by Fritzing 0.9.3b)
circuit board: 11.4653cm x 5.60916cm
breadboards: 1

parts:
  J1 = female pin header, 8 pins [form="♀ (female)"]
  J2 = female pin header, 8 pins [form="♀ (female)"]
  J3 = female pin header, 8 pins [form="♀ (female)"]  # not connected
  J4 = female pin header, 8 pins [form="♀ (female)"]  # not connected
  J5 = female pin header, 8 pins [form="♀ (female)"]  # not connected
  J6 = female pin header, 8 pins [form="♀ (female)"]  # not connected
  U1 = STP16CP05 [package=so-24dw]
  R1 = Resistor [tolerance=±5% resistance=10k package="0805 [SMD]"]
  J7 = Power Jack [package=power_jack_pth]  # not connected

nets:
  N1: J1.pin1, U1.SDO
  N2: J1.pin2, U1.OUT9
  N3: J1.pin3, U1.OUT0
  N4: J1.pin4, U1.OUT12
  N5: J1.pin5, U1.CLK
  N6: J1.pin6, U1.OUT11
  N7: J1.pin7, U1.REXT
  N8: J1.pin8, U1.OUT3
  N9: J2.pin1, U1.OUT2
  N10: J2.pin2, U1.OUT6
  N11: J2.pin3, U1.OUT10
  N12: J2.pin4, U1.~OE
  N13: J2.pin5, U1.SDI
  N14: J2.pin6, U1.OUT15
  N15: J2.pin7, U1.OUT1
  N16: J2.pin8, U1.OUT5
  N17: U1.LE, U1.OUT4
  N18: U1.OUT13, R1.Pin_0
  N19: U1.OUT14, R1.Pin_1
